// Logisim project 16 Bit ALU Final.circ as structural Verilog: 2 circuits, main circuit 1 bit ALU
module _1_bit_ALU (
  input  A,
  input  Sub,
  input  Cin,
  input  B,
  input  Less,
  input  [1:0] Operation,
  output Result,
  output Set,
  output Cout
);

  wire and_1_out, or_1_out, xor_1_out;

  xor xor_1 (xor_1_out, B, Sub);
  and and_1 (and_1_out, A, B);
  or or_1 (or_1_out, A, B);
  Adder #(.width(1)) adder_1 (.a(A), .b(xor_1_out), .out(Set), .cin(Cin), .cout(Cout));
  Multiplexer #(.select(2), .enable("false")) multiplexer_1 (
    .in0(and_1_out), .in1(or_1_out), .in2(Set), .in3(Less), .out(Result), .sel(Operation));
endmodule

module _16_bit_ALU (
  input  Sub,
  input  Cin,
  input  [1:0] Operation,
  input  [15:0] A,
  input  [15:0] B,
  output [15:0] Result,
  output Zero,
  output Cout
);

  wire n1_bit_alu_1_cout, n1_bit_alu_2_cout, n1_bit_alu_3_cout, n1_bit_alu_4_cout, n1_bit_alu_5_cout,
       n1_bit_alu_6_cout, n1_bit_alu_7_cout, n1_bit_alu_8_cout, n1_bit_alu_9_cout, n1_bit_alu_10_cout,
       n1_bit_alu_11_cout, n1_bit_alu_12_cout, n1_bit_alu_13_cout, n1_bit_alu_14_cout, n1_bit_alu_15_cout,
       n1_bit_alu_16_set;

  _1_bit_ALU u_1_bit_alu_1 (
    .A(A[0]), .B(B[0]), .Less(n1_bit_alu_16_set), .Result(Result[0]), .Cout(n1_bit_alu_1_cout), .Sub(Sub),
    .Cin(Cin), .Operation(Operation));  // open: Set
  _1_bit_ALU u_1_bit_alu_2 (
    .A(A[1]), .B(B[1]), .Less(1'b0), .Result(Result[1]), .Cout(n1_bit_alu_2_cout), .Sub(Sub),
    .Cin(n1_bit_alu_1_cout), .Operation(Operation));  // open: Set
  _1_bit_ALU u_1_bit_alu_3 (
    .A(A[2]), .B(B[2]), .Less(1'b0), .Result(Result[2]), .Cout(n1_bit_alu_3_cout), .Sub(Sub),
    .Cin(n1_bit_alu_2_cout), .Operation(Operation));  // open: Set
  _1_bit_ALU u_1_bit_alu_4 (
    .A(A[3]), .B(B[3]), .Less(1'b0), .Result(Result[3]), .Cout(n1_bit_alu_4_cout), .Sub(Sub),
    .Cin(n1_bit_alu_3_cout), .Operation(Operation));  // open: Set
  _1_bit_ALU u_1_bit_alu_5 (
    .A(A[4]), .B(B[4]), .Less(1'b0), .Result(Result[4]), .Cout(n1_bit_alu_5_cout), .Sub(Sub),
    .Cin(n1_bit_alu_4_cout), .Operation(Operation));  // open: Set
  _1_bit_ALU u_1_bit_alu_6 (
    .A(A[5]), .B(B[5]), .Less(1'b0), .Result(Result[5]), .Cout(n1_bit_alu_6_cout), .Sub(Sub),
    .Cin(n1_bit_alu_5_cout), .Operation(Operation));  // open: Set
  _1_bit_ALU u_1_bit_alu_7 (
    .A(A[6]), .B(B[6]), .Less(1'b0), .Result(Result[6]), .Cout(n1_bit_alu_7_cout), .Sub(Sub),
    .Cin(n1_bit_alu_6_cout), .Operation(Operation));  // open: Set
  _1_bit_ALU u_1_bit_alu_8 (
    .A(A[7]), .B(B[7]), .Less(1'b0), .Result(Result[7]), .Cout(n1_bit_alu_8_cout), .Sub(Sub),
    .Cin(n1_bit_alu_7_cout), .Operation(Operation));  // open: Set
  _1_bit_ALU u_1_bit_alu_9 (
    .A(A[8]), .B(B[8]), .Less(1'b0), .Result(Result[8]), .Cout(n1_bit_alu_9_cout), .Sub(Sub),
    .Cin(n1_bit_alu_8_cout), .Operation(Operation));  // open: Set
  _1_bit_ALU u_1_bit_alu_10 (
    .A(A[9]), .B(B[9]), .Less(1'b0), .Result(Result[9]), .Cout(n1_bit_alu_10_cout), .Sub(Sub),
    .Cin(n1_bit_alu_9_cout), .Operation(Operation));  // open: Set
  _1_bit_ALU u_1_bit_alu_11 (
    .A(A[10]), .B(B[10]), .Less(1'b0), .Result(Result[10]), .Cout(n1_bit_alu_11_cout), .Sub(Sub),
    .Cin(n1_bit_alu_10_cout), .Operation(Operation));  // open: Set
  _1_bit_ALU u_1_bit_alu_12 (
    .A(A[11]), .B(B[11]), .Less(1'b0), .Result(Result[11]), .Cout(n1_bit_alu_12_cout), .Sub(Sub),
    .Cin(n1_bit_alu_11_cout), .Operation(Operation));  // open: Set
  _1_bit_ALU u_1_bit_alu_13 (
    .A(A[12]), .B(B[12]), .Less(1'b0), .Result(Result[12]), .Cout(n1_bit_alu_13_cout), .Sub(Sub),
    .Cin(n1_bit_alu_12_cout), .Operation(Operation));  // open: Set
  _1_bit_ALU u_1_bit_alu_14 (
    .A(A[13]), .B(B[13]), .Less(1'b0), .Result(Result[13]), .Cout(n1_bit_alu_14_cout), .Sub(Sub),
    .Cin(n1_bit_alu_13_cout), .Operation(Operation));  // open: Set
  _1_bit_ALU u_1_bit_alu_15 (
    .A(A[14]), .B(B[14]), .Less(1'b0), .Result(Result[14]), .Cout(n1_bit_alu_15_cout), .Sub(Sub),
    .Cin(n1_bit_alu_14_cout), .Operation(Operation));  // open: Set
  _1_bit_ALU u_1_bit_alu_16 (
    .A(A[15]), .B(B[15]), .Less(1'b0), .Result(Result[15]), .Set(n1_bit_alu_16_set), .Cout(Cout), .Sub(Sub),
    .Cin(n1_bit_alu_15_cout), .Operation(Operation));
  nor nor_1 (Zero, Result[0], Result[1], Result[2], Result[3], Result[4], Result[5], Result[6], Result[7], Result[8], Result[9], Result[10], Result[11], Result[12], Result[13], Result[14], Result[15]);
endmodule
