// Logisim project 16-Bit Register File Final.circ as structural Verilog: 2 circuits, main circuit main
module main (
  input  [2:0] Rs,
  input  [2:0] Rt,
  input  [2:0] Rd,
  input  [15:0] Write_Data,
  input  RegWrite,
  output [15:0] Read_Data_Rs,
  output [15:0] Read_Data_Rt
);

  wire Clock_out;

  _16_Bit_Register u_16_bit_register_1 (
    .out_7(Read_Data_Rs), .out_8(Read_Data_Rt), .Clock(Clock_out), .Write_Data(Write_Data),
    .Register_Selector(Rd), .Rs(Rs), .Rt(Rt), .RegWrite(RegWrite));
  Clock Clock (.out(Clock_out));

  // Notes on the sheet:
  //   Register File
  //   Block Diagram For 16-Bit Register File
endmodule

module _16_Bit_Register (
  input  [15:0] Write_Data,
  input  Clock,
  input  RegWrite,
  input  [2:0] Rs,
  input  [2:0] Register_Selector,
  input  [2:0] Rt,
  output [15:0] out_7,
  output [15:0] out_8
);

  wire and_1_out, and_2_out, and_3_out, and_4_out, and_5_out, and_6_out, and_7_out, and_8_out,
       decoder_1_out0, decoder_1_out1, decoder_1_out2, decoder_1_out3, decoder_1_out4, decoder_1_out5,
       decoder_1_out6, decoder_1_out7;
  wire [15:0] register_1_q, register_2_q, register_3_q, register_4_q, register_5_q, register_6_q,
       register_7_q, register_8_q;

  Decoder #(.select(3), .enable("false")) decoder_1 (
    .out0(decoder_1_out0), .out1(decoder_1_out1), .out2(decoder_1_out2), .out3(decoder_1_out3),
    .out4(decoder_1_out4), .out5(decoder_1_out5), .out6(decoder_1_out6), .out7(decoder_1_out7),
    .sel(Register_Selector));
  and and_1 (and_1_out, decoder_1_out0, RegWrite);
  and and_2 (and_2_out, decoder_1_out1, RegWrite);
  and and_3 (and_3_out, decoder_1_out2, RegWrite);
  and and_4 (and_4_out, decoder_1_out3, RegWrite);
  and and_5 (and_5_out, decoder_1_out4, RegWrite);
  and and_6 (and_6_out, decoder_1_out5, RegWrite);
  and and_7 (and_7_out, decoder_1_out6, RegWrite);
  and and_8 (and_8_out, decoder_1_out7, RegWrite);
  Register #(.width(16)) register_1 (.D(Write_Data), .en(and_1_out), .Q(register_1_q), .clk(Clock));  // open: clr
  Register #(.width(16)) register_2 (.D(Write_Data), .en(and_2_out), .Q(register_2_q), .clk(Clock));  // open: clr
  Register #(.width(16)) register_3 (.D(Write_Data), .en(and_3_out), .Q(register_3_q), .clk(Clock));  // open: clr
  Register #(.width(16)) register_4 (.D(Write_Data), .en(and_4_out), .Q(register_4_q), .clk(Clock));  // open: clr
  Register #(.width(16)) register_5 (.D(Write_Data), .en(and_5_out), .Q(register_5_q), .clk(Clock));  // open: clr
  Register #(.width(16)) register_6 (.D(Write_Data), .en(and_6_out), .Q(register_6_q), .clk(Clock));  // open: clr
  Register #(.width(16)) register_7 (.D(Write_Data), .en(and_7_out), .Q(register_7_q), .clk(Clock));  // open: clr
  Register #(.width(16)) register_8 (.D(Write_Data), .en(and_8_out), .Q(register_8_q), .clk(Clock));  // open: clr
  Multiplexer #(.select(3), .width(16), .enable("false")) multiplexer_1 (
    .in0(register_1_q), .in1(register_2_q), .in2(register_3_q), .in3(register_4_q), .in4(register_5_q),
    .in5(register_6_q), .in6(register_7_q), .in7(register_8_q), .out(out_7), .sel(Rs));
  Multiplexer #(.select(3), .width(16), .enable("false")) multiplexer_2 (
    .in0(register_1_q), .in1(register_2_q), .in2(register_3_q), .in3(register_4_q), .in4(register_5_q),
    .in5(register_6_q), .in6(register_7_q), .in7(register_8_q), .out(out_8), .sel(Rt));

  // Notes on the sheet:
  //   16-Bit Register
  //   Read Data From Rs
  //   Read Data From Rt
endmodule
