// Logisim project DataPath.circ as structural Verilog: 3 circuits, main circuit main
module main (
  input  Reset,
  output [2:0] out_2,
  output [2:0] out_3,
  output [2:0] out_4,
  output [15:0] out_5,
  output [15:0] out_6,
  output Cout,
  output out_8,
  output [15:0] out_9,
  output [5:0] out_10,
  output [15:0] out_11
);

  wire and_1_out, Cin, cin_t, clock_1_out, control_unit_1_alusrc, control_unit_1_branch,
       control_unit_1_mem_read, control_unit_1_mem_to_reg, control_unit_1_mem_write, control_unit_1_reg_dst,
       control_unit_1_reg_write;
  wire [1:0] alu_control_1_operation, AOp;
  wire [15:0] adder_1_out, adder_2_out, counter_1_q, multiplexer_2_out, multiplexer_3_out,
       n16_bit_alu_1_result, ram_1_data;
  wire [15:12] rom_1_data;

  Counter #(.width(16), .max('hffff)) counter_1 (
    .D(multiplexer_2_out), .Q(counter_1_q), .clk(clock_1_out), .clr(Reset));  // open: load, count, carry
  Clock clock_1 (.out(clock_1_out));
  Adder #(.width(16)) adder_1 (.a(16'h1), .b(counter_1_q), .out(adder_1_out), .cin(1'b0));  // open: cout
  Control_Unit control_unit_1 (
    .in_1(rom_1_data), .out_9(AOp), .Reg_Dst(control_unit_1_reg_dst), .ALUSrc(control_unit_1_alusrc),
    .Mem_to_Reg(control_unit_1_mem_to_reg), .Reg_Write(control_unit_1_reg_write),
    .Mem_Read(control_unit_1_mem_read), .Mem_Write(control_unit_1_mem_write), .Branch(control_unit_1_branch));
  ROM #(.addrWidth(16), .dataWidth(16)) rom_1 (
    .addr(counter_1_q), .data({rom_1_data, out_2, out_3, out_10[2:0], out_10[5:3]}));  // open: sel
  Multiplexer #(.width(3), .enable("false")) multiplexer_1 (
    .in0(out_3), .in1(out_10[2:0]), .out(out_4), .sel(control_unit_1_reg_dst));
  assign out_11 = {{10{out_10[5]}}, out_10};  // Bit_Extender bit_extender_1
  _16_Bit_Register u_16_bit_register_1 (
    .out_7(out_5), .out_8(out_6), .Clock(clock_1_out), .Write_Data(out_9), .Register_Selector(out_4),
    .Rs(out_2), .Rt(out_3), .RegWrite(control_unit_1_reg_write));
  Adder #(.width(16)) adder_2 (.a(adder_1_out), .b(out_11), .out(adder_2_out));  // open: cin, cout
  and and_1 (and_1_out, control_unit_1_branch, out_8);
  ALU_Control alu_control_1 (.in_1(out_10[5:3]), .ALUOp(AOp), .Operation({Cin, alu_control_1_operation}));
  Multiplexer #(.width(16), .enable("false")) multiplexer_2 (
    .in0(adder_1_out), .in1(adder_2_out), .out(multiplexer_2_out), .sel(and_1_out));
  Multiplexer #(.width(16), .enable("false")) multiplexer_3 (
    .in0(out_6), .in1(out_11), .out(multiplexer_3_out), .sel(control_unit_1_alusrc));
  _16_bit_ALU u_16_bit_alu_1 (
    .A(out_5), .B(multiplexer_3_out), .Result(n16_bit_alu_1_result), .Zero(out_8), .Cout(Cout), .Sub(Cin),
    .Cin(cin_t), .Operation(alu_control_1_operation));
  RAM #(.addrWidth(16), .dataWidth(16), .bus("separate")) ram_1 (
    .addr(n16_bit_alu_1_result), .din(out_6), .data(ram_1_data), .str(control_unit_1_mem_write),
    .clk(clock_1_out), .ld(control_unit_1_mem_read));  // open: sel, clr
  Multiplexer #(.width(16), .enable("false")) multiplexer_4 (
    .in0(n16_bit_alu_1_result), .in1(ram_1_data), .out(out_9), .sel(control_unit_1_mem_to_reg));

  // Notes on the sheet:
  //   PC
  //   Clk
  //   contents of rom_1 (hex, n*v repeats v):
  //   b1c0 50 c4c5
  //   Reg Dst
  //   Regwrite
  //   Alu Src
  //   Flag Zero
  //   Mem Write
  //   Mem Read
  //   Mem to Reg
endmodule

module Control_Unit (
  input  [3:0] in_1,
  output Reg_Dst,
  output ALUSrc,
  output Mem_to_Reg,
  output Reg_Write,
  output Mem_Read,
  output Mem_Write,
  output Branch,
  output [1:0] out_9
);

  wire and_5_out;

  and and_1 (out_9[1], ~in_1[3], ~in_1[2], ~in_1[1], ~in_1[0]);  // AND_Gate
  and and_2 (Mem_Read, in_1[3], ~in_1[2], in_1[1], in_1[0]);  // AND_Gate
  and and_3 (Mem_Write, in_1[3], ~in_1[2], ~in_1[1], in_1[0]);  // AND_Gate
  and and_4 (Branch, ~in_1[3], in_1[2], ~in_1[1], ~in_1[0]);  // AND_Gate
  and and_5 (and_5_out, in_1[3], in_1[2], ~in_1[1], ~in_1[0]);  // AND_Gate
  or or_1 (ALUSrc, Mem_Read, and_5_out, Mem_Write);
  or or_2 (Reg_Write, out_9[1], and_5_out, Mem_Read);

  assign Mem_to_Reg = Mem_Read;
  assign out_9[0] = 1'b0;
  assign Reg_Dst = out_9[1];
endmodule

module ALU_Control (
  input  [2:0] in_1,
  input  [1:0] ALUOp,
  output [2:0] Operation
);

  wire and_1_out;

  and and_1 (and_1_out, in_1[1], ALUOp[1]);
  or or_1 (Operation[2], and_1_out, ALUOp[0]);
  or or_2 (Operation[1], ~ALUOp[1], ~in_1[2]);  // OR_Gate
  and and_2 (Operation[0], in_1[0], ALUOp[1]);

  // Notes on the sheet:
  //   Function
endmodule
